# Fritzing sketch morse (saved by Fritzing 0.9.2b)
breadboards: 1

parts:
  Componente1 = Bluetooth HC-06
  J1 = Piezo Speaker
  LED1 = smd LED [color="Red (633nm)" package="0603 [SMD]"]
  LCD2 = LCD screen  # not connected
  LCM1602_IIC1 = LCM1602 IIC [part_number="LCM1602 IIC" chip_label="LCM1602 IIC" package="DIP (Dual Inline) [THT]"]
  Componente2 = Arduino Uno (Rev3)
  R1 = Resistor [tolerance=±5% resistance=330 package="2010 [SMD]"]

nets:
  N1: Componente1.TXD, Componente2.D0/RX
  GND: Componente1.GND, J1.pin1, LED1.cathode, LCM1602_IIC1.GND, Componente2.GND
  VCC: Componente1.VCC, LCM1602_IIC1.VCC, Componente2.5V
  N2: J1.pin2, Componente2.D9_PWM
  N3: LED1.anode, Componente2.D8
  N4: LCM1602_IIC1.SDA, Componente2.A4/SDA
  N5: LCM1602_IIC1.SCL, Componente2.A5/SCL
  N6: Componente2.D1/TX, R1.Pin_1

custom parts:
  LCM1602 IIC: I2C-Module to use a 1602 or 2004 LCD on with the wire.h libory Serial LCD Modul
